// Logisim project computer_8bits.circ as structural Verilog: 4 circuits, main circuit main
module main (
  input  in_1,
  input  in_2,
  input  in_3,
  input  in_4,
  input  in_5,
  input  in_6,
  input  in_7,
  input  in_8,
  input  EA,
  input  LA,
  input  CA,
  input  EB,
  input  LB,
  input  CB,
  input  EL,
  input  SL
);

  wire alu_1_s0, alu_1_s1, alu_1_s2, alu_1_s3, alu_1_s4, alu_1_s5, alu_1_s6, alu_1_s7, clock_1_out,
       register_1_b0, register_1_b1, register_1_b2, register_1_b3, register_1_b4, register_1_b5,
       register_1_b6, register_1_b7, register_2_b0, register_2_b1, register_2_b2, register_2_b3,
       register_2_b4, register_2_b5, register_2_b6, register_2_b7;

  Clock clock_1 (.out(clock_1_out));
  DotMatrix #(.matrixcols(8), .matrixrows(1), .dotshape("circle")) dotmatrix_1 (
    .col0(in_1), .col1(in_2), .col2(in_3), .col3(in_4), .col4(in_5), .col5(in_6), .col6(in_7), .col7(in_8));
  Register register_1 (
    .I7(in_1), .I6(in_2), .I5(in_3), .I4(in_4), .I3(in_5), .I2(in_6), .I1(in_7), .I0(in_8), .O7(in_1),
    .O6(in_2), .O5(in_3), .O4(in_4), .O3(in_5), .O2(in_6), .O1(in_7), .O0(in_8), .Clock(clock_1_out), .L(LA),
    .Clear(CA), .E(EA), .B7(register_1_b7), .B6(register_1_b6), .B5(register_1_b5), .B4(register_1_b4),
    .B3(register_1_b3), .B2(register_1_b2), .B1(register_1_b1), .B0(register_1_b0));
  DotMatrix #(.inputtype("row"), .matrixcols(1), .matrixrows(8), .dotshape("circle")) dotmatrix_2 (
    .row0(register_1_b0), .row1(register_1_b1), .row2(register_1_b2), .row3(register_1_b3),
    .row4(register_1_b4), .row5(register_1_b5), .row6(register_1_b6), .row7(register_1_b7));
  Register register_2 (
    .I7(in_1), .I6(in_2), .I5(in_3), .I4(in_4), .I3(in_5), .I2(in_6), .I1(in_7), .I0(in_8), .O7(in_1),
    .O6(in_2), .O5(in_3), .O4(in_4), .O3(in_5), .O2(in_6), .O1(in_7), .O0(in_8), .Clock(clock_1_out), .L(LB),
    .Clear(CB), .E(EB), .B7(register_2_b7), .B6(register_2_b6), .B5(register_2_b5), .B4(register_2_b4),
    .B3(register_2_b3), .B2(register_2_b2), .B1(register_2_b1), .B0(register_2_b0));
  DotMatrix #(.inputtype("row"), .matrixcols(1), .matrixrows(8), .dotshape("circle")) dotmatrix_3 (
    .row0(register_2_b0), .row1(register_2_b1), .row2(register_2_b2), .row3(register_2_b3),
    .row4(register_2_b4), .row5(register_2_b5), .row6(register_2_b6), .row7(register_2_b7));
  ALU alu_1 (
    .E0(in_8), .E1(in_7), .E2(in_6), .E3(in_5), .E4(in_4), .E5(in_3), .E6(in_2), .E7(in_1), .Su(SL),
    .A7(register_1_b7), .A6(register_1_b6), .A5(register_1_b5), .A4(register_1_b4), .A3(register_1_b3),
    .A2(register_1_b2), .A1(register_1_b1), .A0(register_1_b0), .S7(alu_1_s7), .S6(alu_1_s6), .S5(alu_1_s5),
    .S4(alu_1_s4), .S3(alu_1_s3), .S2(alu_1_s2), .S1(alu_1_s1), .S0(alu_1_s0), .En(EL), .B7(register_2_b7),
    .B6(register_2_b6), .B5(register_2_b5), .B4(register_2_b4), .B3(register_2_b3), .B2(register_2_b2),
    .B1(register_2_b1), .B0(register_2_b0));  // open: CO
  DotMatrix #(.inputtype("row"), .matrixcols(1), .matrixrows(8), .dotshape("circle")) dotmatrix_4 (
    .row0(alu_1_s0), .row1(alu_1_s1), .row2(alu_1_s2), .row3(alu_1_s3), .row4(alu_1_s4), .row5(alu_1_s5),
    .row6(alu_1_s6), .row7(alu_1_s7));

  // Notes on the sheet:
  //   BUS
  //   Register A
  //   Register B
endmodule

module Register (
  input  Clock,
  input  L,
  input  Clear,
  input  E,
  input  I7,
  input  I6,
  input  I5,
  input  I4,
  input  I3,
  input  I2,
  input  I1,
  input  I0,
  output B7,
  output B6,
  output B5,
  output B4,
  output B3,
  output B2,
  output B1,
  output B0,
  output O7,
  output O6,
  output O5,
  output O4,
  output O3,
  output O2,
  output O1,
  output O0
);

  Register_part #(.width(1)) register_1 (.D(I7), .en(L), .Q(B7), .clk(Clock), .clr(Clear));
  Register_part #(.width(1)) register_2 (.D(I6), .en(L), .Q(B6), .clk(Clock), .clr(Clear));
  Register_part #(.width(1)) register_3 (.D(I5), .en(L), .Q(B5), .clk(Clock), .clr(Clear));
  Register_part #(.width(1)) register_4 (.D(I4), .en(L), .Q(B4), .clk(Clock), .clr(Clear));
  Register_part #(.width(1)) register_5 (.D(I3), .en(L), .Q(B3), .clk(Clock), .clr(Clear));
  Register_part #(.width(1)) register_6 (.D(I2), .en(L), .Q(B2), .clk(Clock), .clr(Clear));
  Register_part #(.width(1)) register_7 (.D(I1), .en(L), .Q(B1), .clk(Clock), .clr(Clear));
  Register_part #(.width(1)) register_8 (.D(I0), .en(L), .Q(B0), .clk(Clock), .clr(Clear));
  assign O7 = E ? B7 : 1'bz;  // Controlled_Buffer controlled_buffer_1
  assign O6 = E ? B6 : 1'bz;  // Controlled_Buffer controlled_buffer_2
  assign O5 = E ? B5 : 1'bz;  // Controlled_Buffer controlled_buffer_3
  assign O4 = E ? B4 : 1'bz;  // Controlled_Buffer controlled_buffer_4
  assign O3 = E ? B3 : 1'bz;  // Controlled_Buffer controlled_buffer_5
  assign O2 = E ? B2 : 1'bz;  // Controlled_Buffer controlled_buffer_6
  assign O1 = E ? B1 : 1'bz;  // Controlled_Buffer controlled_buffer_7
  assign O0 = E ? B0 : 1'bz;  // Controlled_Buffer controlled_buffer_8
endmodule

module Full_adder (
  input  A,
  input  B,
  input  Ci,
  output E,
  output Co
);

  wire and_1_out, and_2_out, xor_1_out;

  xor xor_1 (xor_1_out, A, B);
  and and_1 (and_1_out, xor_1_out, Ci);
  and and_2 (and_2_out, A, B);
  xor xor_2 (E, xor_1_out, Ci);
  or or_1 (Co, and_1_out, and_2_out);
endmodule

module ALU (
  input  Su,
  input  A7,
  input  A6,
  input  A5,
  input  A4,
  input  A3,
  input  A2,
  input  A1,
  input  A0,
  input  En,
  input  B7,
  input  B6,
  input  B5,
  input  B4,
  input  B3,
  input  B2,
  input  B1,
  input  B0,
  output CO,
  output S7,
  output S6,
  output S5,
  output S4,
  output S3,
  output S2,
  output S1,
  output S0,
  output E0,
  output E1,
  output E2,
  output E3,
  output E4,
  output E5,
  output E6,
  output E7
);

  wire full_adder_1_co, full_adder_2_co, full_adder_3_co, full_adder_4_co, full_adder_5_co, full_adder_6_co,
       full_adder_7_co, xor_1_out, xor_2_out, xor_3_out, xor_4_out, xor_5_out, xor_6_out, xor_7_out,
       xor_8_out;

  Full_adder full_adder_1 (.B(xor_7_out), .Ci(Su), .E(S0), .Co(full_adder_1_co), .A(A0));
  Full_adder full_adder_2 (.B(xor_6_out), .Ci(full_adder_3_co), .E(S2), .Co(full_adder_2_co), .A(A2));
  Full_adder full_adder_3 (.B(xor_8_out), .Ci(full_adder_1_co), .E(S1), .Co(full_adder_3_co), .A(A1));
  xor xor_1 (xor_1_out, Su, B7);
  xor xor_2 (xor_2_out, Su, B6);
  Full_adder full_adder_4 (.B(xor_5_out), .Ci(full_adder_2_co), .E(S3), .Co(full_adder_4_co), .A(A3));
  xor xor_3 (xor_3_out, Su, B4);
  xor xor_4 (xor_4_out, Su, B5);
  Full_adder full_adder_5 (.B(xor_3_out), .Ci(full_adder_4_co), .E(S4), .Co(full_adder_5_co), .A(A4));
  xor xor_5 (xor_5_out, Su, B3);
  xor xor_6 (xor_6_out, Su, B2);
  Full_adder full_adder_6 (.B(xor_2_out), .Ci(full_adder_7_co), .E(S6), .Co(full_adder_6_co), .A(A6));
  Full_adder full_adder_7 (.B(xor_4_out), .Ci(full_adder_5_co), .E(S5), .Co(full_adder_7_co), .A(A5));
  xor xor_7 (xor_7_out, Su, B0);
  xor xor_8 (xor_8_out, Su, B1);
  Full_adder full_adder_8 (.B(xor_1_out), .Ci(full_adder_6_co), .E(S7), .Co(CO), .A(A7));
  assign E0 = En ? S0 : 1'bz;  // Controlled_Buffer controlled_buffer_1
  assign E1 = En ? S2 : 1'bz;  // Controlled_Buffer controlled_buffer_2
  assign E2 = En ? S2 : 1'bz;  // Controlled_Buffer controlled_buffer_3
  assign E3 = En ? S3 : 1'bz;  // Controlled_Buffer controlled_buffer_4
  assign E4 = En ? S4 : 1'bz;  // Controlled_Buffer controlled_buffer_5
  assign E5 = En ? S5 : 1'bz;  // Controlled_Buffer controlled_buffer_6
  assign E6 = En ? S6 : 1'bz;  // Controlled_Buffer controlled_buffer_7
  assign E7 = En ? S7 : 1'bz;  // Controlled_Buffer controlled_buffer_8
endmodule
